// Logisim project SLC1_Design.circ as structural Verilog: 8 circuits, main circuit main
module main (
  input  in_1,
  input  in_2,
  input  in_3,
  input  in_4,
  input  in_5,
  output [1:0] out_6,
  output [15:0] PC,
  output [15:0] IR,
  output [2:0] out_9,
  output [2:0] out_10,
  output [7:0] out_11
);

  wire clock_1_out, decode_1_is_add, decode_1_is_alu, decode_1_is_and, decode_1_is_branch,
       decode_1_is_immediate, decode_1_is_load, decode_1_is_move, decode_1_is_nop, decode_1_is_not,
       decode_1_is_or, decode_1_is_ret, decode_1_is_shift, decode_1_is_shl, decode_1_is_shr,
       decode_1_is_store, decode_1_is_sub, decode_1_is_trap, decode_1_is_xor;
  wire [2:0] decode_1_branch_nzp;
  wire [8:0] decode_1_imm9;
  wire [9:0] decode_1_imm10;
  wire [11:0] decode_1_imm12;
  wire [15:0] mem_1_mem_out;

  Clock clock_1 (.out(clock_1_out));
  mem mem_1 (.mem_addr(PC), .mem_w(in_4), .mem_output_en(in_5), .clk(clock_1_out), .mem_out(mem_1_mem_out));
  fetch fetch_1 (
    .ir_in(mem_1_mem_out), .pc_w(in_1), .ir_w(in_2), .pc_mux_sel({in_3, 1'b0}), .clk(clock_1_out), .pc(PC),
    .ir(IR));
  decode decode_1 (
    .ir(IR), .is_alu(decode_1_is_alu), .is_add(decode_1_is_add), .is_sub(decode_1_is_sub),
    .is_and(decode_1_is_and), .is_or(decode_1_is_or), .is_xor(decode_1_is_xor), .is_not(decode_1_is_not),
    .is_immediate(decode_1_is_immediate), .is_move(decode_1_is_move), .is_shift(decode_1_is_shift),
    .is_shl(decode_1_is_shl), .is_shr(decode_1_is_shr), .is_store(decode_1_is_store),
    .is_load(decode_1_is_load), .is_branch(decode_1_is_branch), .branch_nzp(decode_1_branch_nzp),
    .is_trap(decode_1_is_trap), .is_ret(decode_1_is_ret), .is_nop(decode_1_is_nop), .src1(out_9),
    .src2(out_10), .imm8(out_11), .imm9(decode_1_imm9), .imm10(decode_1_imm10), .imm12(decode_1_imm12));
  execute execute_1 (
    .clk(clock_1_out), .PC(PC), .branch_nzp(decode_1_branch_nzp), .is_immediate(decode_1_is_immediate),
    .src1(out_9), .src2(out_10), .imm8(out_11), .imm9(decode_1_imm9), .imm10(decode_1_imm10),
    .imm12(decode_1_imm12), .is_alu(decode_1_is_alu), .is_shift(decode_1_is_shift),
    .is_move(decode_1_is_move), .is_store(decode_1_is_store), .is_load(decode_1_is_load),
    .is_branch(decode_1_is_branch), .is_trap(decode_1_is_trap), .is_ret(decode_1_is_ret),
    .is_add(decode_1_is_add), .is_sub(decode_1_is_sub), .is_and(decode_1_is_and), .is_or(decode_1_is_or),
    .is_xor(decode_1_is_xor), .is_not(decode_1_is_not), .is_shl(decode_1_is_shl), .is_shr(decode_1_is_shr),
    .is_nop(decode_1_is_nop));

  assign out_6 = {in_3, 1'b0};

  // Notes on the sheet:
  //   in_5: initial=0x1
  //   in_1: initial=0x1
  //   in_2: initial=0x1
  //   in_3: initial=0x1
endmodule

module fetch (
  input  [15:0] ir_in,
  input  pc_w,
  input  ir_w,
  input  [1:0] pc_mux_sel,
  input  clk,
  output [15:0] pc,
  output [15:0] ir
);

  wire [15:0] adder_1_out, multiplexer_1_out, undriven;

  Adder #(.width(16)) adder_1 (.a(pc), .b(16'h1), .out(adder_1_out));  // open: cin, cout
  Multiplexer #(.select(2), .width(16)) multiplexer_1 (
    .in0(adder_1_out), .in1(undriven), .in2(16'h8000), .in3(16'h8000), .out(multiplexer_1_out),
    .sel(pc_mux_sel));
  Register #(.width(16)) Program_Counter (.D(multiplexer_1_out), .en(pc_w), .clk(clk), .Q(pc));  // open: clr
  Register #(.width(16)) Instruction_Register (.D(ir_in), .en(ir_w), .clk(clk), .Q(ir));  // open: clr
endmodule

module decode (
  input  [15:0] ir,
  output is_alu,
  output is_add,
  output is_sub,
  output is_and,
  output is_or,
  output is_xor,
  output is_not,
  output is_immediate,
  output is_move,
  output is_shift,
  output is_shl,
  output is_shr,
  output is_store,
  output is_load,
  output is_branch,
  output [2:0] branch_nzp,
  output is_trap,
  output is_ret,
  output is_nop,
  output [2:0] src1,
  output [2:0] src2,
  output [7:0] imm8,
  output [8:0] imm9,
  output [9:0] imm10,
  output [11:0] imm12
);

  wire decoder_1_out0, decoder_1_out1, decoder_1_out7, not_1_out, not_2_out, not_3_out, not_4_out, not_5_out,
       not_6_out, not_7_out, not_8_out;

  Decoder #(.enable("false"), .select(3)) decoder_1 (
    .out0(decoder_1_out0), .out1(decoder_1_out1), .out2(is_move), .out3(is_shift), .out4(is_store),
    .out5(is_load), .out6(is_branch), .out7(decoder_1_out7), .sel(ir[15:13]));
  and and_1 (is_add, decoder_1_out0, not_1_out);
  not not_1 (not_1_out, ir[0]);
  and and_2 (is_sub, decoder_1_out0, ir[0]);
  not not_2 (not_2_out, ir[0]);
  and and_3 (is_shl, is_shift, not_2_out);
  and and_4 (is_shr, is_shift, ir[0]);
  and and_5 (is_and, decoder_1_out1, not_3_out, not_4_out);
  not not_3 (not_3_out, ir[1]);
  not not_4 (not_4_out, ir[0]);
  and and_6 (is_or, decoder_1_out1, not_5_out, ir[0]);
  not not_5 (not_5_out, ir[1]);
  and and_7 (is_xor, decoder_1_out1, ir[1], not_6_out);
  not not_6 (not_6_out, ir[0]);
  and and_8 (is_not, decoder_1_out1, ir[1], ir[0]);
  not not_7 (not_7_out, ir[12]);
  not not_8 (not_8_out, ir[0]);
  or or_1 (is_alu, decoder_1_out0, decoder_1_out1);
  and and_9 (is_trap, decoder_1_out7, not_7_out);
  and and_10 (is_ret, decoder_1_out7, ir[12], not_8_out);
  and and_11 (is_nop, decoder_1_out7, ir[12], ir[0]);
  not not_9 (is_immediate, ir[12]);

  assign branch_nzp = ir[2:0];
  assign imm8 = ir[8:1];
  assign imm9 = ir[8:0];
  assign imm10 = ir[12:3];
  assign imm12 = ir[11:0];
  assign src1 = ir[11:9];
  assign src2 = ir[8:6];

  // Notes on the sheet:
  //   ir: initial=0xf001
endmodule

module mem (
  input  [15:0] mem_addr,
  input  mem_w,
  input  mem_output_en,
  input  clk,
  output [15:0] mem_out
);

  ROM #(.addrWidth(16), .dataWidth(16)) rom_1 (.addr(mem_addr), .data(mem_out));
  RAM #(.addrWidth(16), .dataWidth(16)) ram_1 ();  // open: addr, we, oe, clk, din, dout

  // Notes on the sheet:
  //   contents of rom_1 (hex, n*v repeats v):
  //   32768*0 614 615 6c0 6c1
endmodule

module execute (
  input  clk,
  input  [15:0] PC,
  input  [2:0] branch_nzp,
  input  is_immediate,
  input  [2:0] src1,
  input  [2:0] src2,
  input  [7:0] imm8,
  input  [8:0] imm9,
  input  [9:0] imm10,
  input  [11:0] imm12,
  input  is_alu,
  input  is_shift,
  input  is_move,
  input  is_store,
  input  is_load,
  input  is_branch,
  input  is_trap,
  input  is_ret,
  input  is_add,
  input  is_sub,
  input  is_and,
  input  is_or,
  input  is_xor,
  input  is_not,
  input  is_shl,
  input  is_shr,
  input  is_nop
);

  wire not_1_out, or_1_out, or_2_out, or_3_out, or_4_out;
  wire [2:0] priority_encoder_1_out;
  wire [15:0] alu_1_alu_out, imm_sign_extender_1_imm8, imm_sign_extender_1_imm12, imm_sign_extender_1_sext8,
       imm_sign_extender_1_sext9, imm_sign_extender_1_sext10, multiplexer_1_out, multiplexer_2_out,
       multiplexer_3_out, op1_q, op2_q, register_file_1_src1_data, register_file_1_src2_data;

  or or_1 (or_1_out, is_alu, is_shift, is_move);
  or or_2 (or_2_out, is_store, is_load, is_branch);
  or or_3 (or_3_out, is_move, is_store, is_load);
  or or_4 (or_4_out, is_sub, is_add);
  imm_sign_extender imm_sign_extender_1 (
    .imm8_in(imm8), .imm9_in(imm9), .imm10_in(imm10), .imm12_in(imm12), .sext8(imm_sign_extender_1_sext8),
    .imm8(imm_sign_extender_1_imm8), .sext9(imm_sign_extender_1_sext9), .sext10(imm_sign_extender_1_sext10),
    .imm12(imm_sign_extender_1_imm12));
  Priority_Encoder priority_encoder_1 (
    .in0(or_4_out), .in1(is_shift), .in2(or_3_out), .in3(is_branch), .in4(is_trap),
    .out(priority_encoder_1_out));  // open: in5, in6, in7, en_in, gs, en_out
  register_file register_file_1 (
    .wr_en(or_1_out), .data_in(alu_1_alu_out), .src1(src1), .src2(src2), .clk(clk),
    .src1_data(register_file_1_src1_data), .src2_data(register_file_1_src2_data));
  Multiplexer #(.width(16)) multiplexer_1 (
    .in0(PC), .in1(register_file_1_src1_data), .out(multiplexer_1_out), .sel(not_1_out));
  not not_1 (not_1_out, or_2_out);
  Multiplexer #(.width(16)) multiplexer_2 (
    .in0(register_file_1_src2_data), .in1(multiplexer_3_out), .out(multiplexer_2_out), .sel(is_immediate));
  Multiplexer #(.select(3), .width(16)) multiplexer_3 (
    .in1(imm_sign_extender_1_sext8), .in2(imm_sign_extender_1_imm8), .in3(imm_sign_extender_1_sext9),
    .in4(imm_sign_extender_1_sext10), .in5(imm_sign_extender_1_imm12), .out(multiplexer_3_out),
    .sel(priority_encoder_1_out));  // open: in0, in6, in7
  Register #(.width(16)) op1 (.D(multiplexer_1_out), .en(1'b1), .clk(clk), .Q(op1_q));  // open: clr
  Register #(.width(16)) op2 (.D(multiplexer_2_out), .en(1'b1), .clk(clk), .Q(op2_q));  // open: clr
  alu alu_1 (
    .op1(op1_q), .op2(op2_q), .is_add(is_add), .is_sub(is_sub), .is_and(is_and), .is_or(is_or),
    .is_xor(is_xor), .is_not(is_not), .is_move(is_move), .is_shift(is_shift), .is_shl(is_shl),
    .is_shr(is_shr), .alu_out(alu_1_alu_out));
endmodule

module alu (
  input  [15:0] op1,
  input  [15:0] op2,
  input  is_add,
  input  is_sub,
  input  is_and,
  input  is_or,
  input  is_xor,
  input  is_not,
  input  is_move,
  input  is_shift,
  input  is_shl,
  input  is_shr,
  output [15:0] alu_out
);

  wire [2:0] priority_encoder_1_out;
  wire [15:0] adder_1_out, and_1_out, multiplexer_1_out, not_1_out, or_1_out, shifter_1_out, shifter_2_out,
       subtractor_1_out, xor_1_out;

  Priority_Encoder priority_encoder_1 (
    .in0(is_add), .in1(is_sub), .in2(is_and), .in3(is_or), .in4(is_xor), .in5(is_not), .in6(is_move),
    .in7(is_shift), .out(priority_encoder_1_out));  // open: en_in, gs, en_out
  Shifter #(.width(16)) shifter_1 (.in(op1), .\dist (op2[3:0]), .out(shifter_1_out));
  Shifter #(.shift("ar"), .width(16)) shifter_2 (.in(op1), .\dist (op2[3:0]), .out(shifter_2_out));
  Adder #(.width(16)) adder_1 (.a(op1), .b(op2), .out(adder_1_out));  // open: cin, cout
  Subtractor #(.width(16)) subtractor_1 (.a(op1), .b(op1), .out(subtractor_1_out));  // open: bin, bout
  assign and_1_out = op1 & op2;  // AND_Gate and_1, 16 bits wide
  assign or_1_out = op1 | op2;  // OR_Gate or_1, 16 bits wide
  assign xor_1_out = op1 ^ op2;  // XOR_Gate xor_1, 16 bits wide
  assign not_1_out = ~op1;  // NOT_Gate not_1, 16 bits wide
  Multiplexer #(.width(16)) multiplexer_1 (
    .in0(shifter_1_out), .in1(shifter_2_out), .out(multiplexer_1_out), .sel(is_shr));
  Multiplexer #(.select(3), .width(16)) multiplexer_2 (
    .in0(adder_1_out), .in1(subtractor_1_out), .in2(and_1_out), .in3(or_1_out), .in4(xor_1_out),
    .in5(not_1_out), .in6(op2), .in7(multiplexer_1_out), .out(alu_out), .sel(priority_encoder_1_out));
endmodule

module register_file (
  input  wr_en,
  input  [15:0] data_in,
  input  [2:0] src1,
  input  [2:0] src2,
  input  clk,
  output [15:0] src1_data,
  output [15:0] src2_data
);

  wire and_1_out, and_2_out, and_3_out, and_4_out, and_5_out, and_6_out, and_7_out, and_8_out,
       decoder_1_out0, decoder_1_out1, decoder_1_out2, decoder_1_out3, decoder_1_out4, decoder_1_out5,
       decoder_1_out6, decoder_1_out7;
  wire [15:0] demultiplexer_1_out0, demultiplexer_1_out1, demultiplexer_1_out2, demultiplexer_1_out3,
       demultiplexer_1_out4, demultiplexer_1_out5, demultiplexer_1_out6, demultiplexer_1_out7, R0_q, R1_q,
       R2_q, R3_q, R4_q, R5_q, R6_q, R7_q;

  Demultiplexer #(.select(3), .width(16)) demultiplexer_1 (
    .out0(demultiplexer_1_out0), .out1(demultiplexer_1_out1), .out2(demultiplexer_1_out2),
    .out3(demultiplexer_1_out3), .out4(demultiplexer_1_out4), .out5(demultiplexer_1_out5),
    .out6(demultiplexer_1_out6), .out7(demultiplexer_1_out7), .in(data_in), .sel(src1));
  Decoder #(.enable("false"), .select(3)) decoder_1 (
    .out0(decoder_1_out0), .out1(decoder_1_out1), .out2(decoder_1_out2), .out3(decoder_1_out3),
    .out4(decoder_1_out4), .out5(decoder_1_out5), .out6(decoder_1_out6), .out7(decoder_1_out7), .sel(src1));
  Register #(.width(16)) R0 (.D(demultiplexer_1_out0), .en(and_1_out), .clk(clk), .Q(R0_q));  // open: clr
  and and_1 (and_1_out, wr_en, decoder_1_out0);
  Register #(.width(16)) R1 (.D(demultiplexer_1_out1), .en(and_2_out), .clk(clk), .Q(R1_q));  // open: clr
  and and_2 (and_2_out, wr_en, decoder_1_out1);
  Register #(.width(16)) R2 (.D(demultiplexer_1_out2), .en(and_3_out), .clk(clk), .Q(R2_q));  // open: clr
  and and_3 (and_3_out, wr_en, decoder_1_out2);
  Register #(.width(16)) R3 (.D(demultiplexer_1_out3), .en(and_4_out), .clk(clk), .Q(R3_q));  // open: clr
  and and_4 (and_4_out, wr_en, decoder_1_out3);
  Register #(.width(16)) R4 (.D(demultiplexer_1_out4), .en(and_5_out), .clk(clk), .Q(R4_q));  // open: clr
  and and_5 (and_5_out, wr_en, decoder_1_out4);
  Register #(.width(16)) R5 (.D(demultiplexer_1_out5), .en(and_6_out), .clk(clk), .Q(R5_q));  // open: clr
  and and_6 (and_6_out, wr_en, decoder_1_out5);
  Register #(.width(16)) R6 (.D(demultiplexer_1_out6), .en(and_7_out), .clk(clk), .Q(R6_q));  // open: clr
  and and_7 (and_7_out, wr_en, decoder_1_out6);
  Register #(.width(16)) R7 (.D(demultiplexer_1_out7), .en(and_8_out), .clk(clk), .Q(R7_q));  // open: clr
  and and_8 (and_8_out, wr_en, decoder_1_out7);
  Multiplexer #(.select(3), .width(16)) multiplexer_1 (
    .in0(R0_q), .in1(R1_q), .in2(R2_q), .in3(R3_q), .in4(R4_q), .in5(R5_q), .in6(R6_q), .in7(R7_q),
    .out(src1_data), .sel(src1));
  Multiplexer #(.select(3), .width(16)) multiplexer_2 (
    .in0(R0_q), .in1(R1_q), .in2(R2_q), .in3(R3_q), .in4(R4_q), .in5(R5_q), .in6(R6_q), .in7(R7_q),
    .out(src2_data), .sel(src2));
endmodule

module imm_sign_extender (
  input  [7:0] imm8_in,
  input  [8:0] imm9_in,
  input  [9:0] imm10_in,
  input  [11:0] imm12_in,
  output [15:0] sext8,
  output [15:0] imm8,
  output [15:0] sext9,
  output [15:0] sext10,
  output [15:0] imm12
);


  assign imm8 = {imm8_in, {8{1'b0}}};
  assign imm12 = {imm12_in[11:2], {2{imm12_in[2]}}, 4'b0000};
  assign imm12_in[1:0] = {2{imm12_in[2]}};
  assign sext8 = {imm8_in, {8{imm8_in[0]}}};
  assign sext9 = {imm9_in, {7{imm9_in[0]}}};
  assign sext10 = {imm10_in, {6{imm10_in[0]}}};

  // Notes on the sheet:
  //   sext8
  //   imm8
  //   sext9
  //   imm9
  //   sext10
  //   imm10
  //   sext12
  //   imm12
endmodule
